# Fritzing sketch Button (saved by Fritzing 0.8.6b)
circuit board: 6.88566cm x 5.36311cm
breadboards: 1

parts:
  S1 = Pushbutton [package=THT]
  R1 = Resistor [tolerance=±5% resistance=10k package=THT]
  Arduino1 = Arduino Uno (Rev3)
  LED1 = LED - 5mm [color="Red (633nm)" package="5 mm [THT]"]
  part = LED - 5mm [color="Red (633nm)" package="5 mm [THT]"]  # not connected

nets:
  N1: S1.leg0, R1.Pin_0, Arduino1.D2
  N2: S1.leg1, Arduino1.5V
  N3: R1.Pin_1, Arduino1.GND, LED1.cathode
  N4: Arduino1.D13/SCK, LED1.anode

notes:
  In this example, a pushbutton is used as a digital input and an LED is a digital output.
  Related example: http://arduino.cc/en/Tutorial/Button
