# Fritzing sketch TouchSwitch (saved by Fritzing 0.8.0b)
breadboards: 2

parts:
  Arduino1 = Arduino Uno (Rev3)
  Q6 = NPN-Transistor [package="TO92 [THT]"]
  Q7 = NPN-Transistor [package="TO92 [THT]"]
  R11 = Resistor [resistance=10k tolerance=±5% package=THT]
  R12 = Resistor [resistance=1k tolerance=±5% package=THT]
  R13 = Resistor [resistance=10k tolerance=±5% package=THT]
  J1 = female pin header, 1 pin [form="♀ (female)"]
  J2 = female pin header, 1 pin [form="♀ (female)"]

nets:
  N1: Arduino1.A0, Q7.E, R13.Pin_0
  N2: Arduino1.5V, R12.Pin_1, R13.Pin_1, J2.pin1
  N3: Arduino1.GND, Q7.C
  N4: Q6.E, R12.Pin_0
  N5: Q6.B, J1.pin1
  N6: Q6.C, R11.Pin_0
  N7: Q7.B, R11.Pin_1

notes:
  A simple touch switch can be created by using two NPN transistors. When touching the two blue cables, the LED will turn on. (download code from the project page)
  http://en.wikipedia.org/wiki/Darlington_transistor
