# Fritzing sketch Countdown (saved by Fritzing 0.8.6b)
circuit board: 6.88566cm x 5.36311cm
breadboards: 2

parts:
  Segment1 = 7 Segment Display
  Segment2 = 7 Segment Display
  R1 = Resistor [tolerance=±5% resistance=1k package=THT]
  R2 = Resistor [tolerance=±5% resistance=1k package=THT]
  R3 = Resistor [tolerance=±5% resistance=1k package=THT]
  R4 = Resistor [tolerance=±5% resistance=1k package=THT]
  S1 = Pushbutton [package="[THT]"]
  R5 = Resistor [tolerance=±5% resistance=10k package=THT]
  Q3 = PNP-Transistor [package="TO92 [THT]"]
  Q2 = PNP-Transistor [package="TO92 [THT]"]
  Q4 = NPN-Transistor [package="TO92 [THT]"]
  Q1 = NPN-Transistor [package="TO92 [THT]"]
  R6 = Rotary Potentiometer (Small) [maximum_resistance=100kΩ package=THT]
  Arduino1 = Arduino Uno (Rev3)
  part = NPN-Transistor [package="TO92 [THT]"]  # not connected

nets:
  N1: Segment1.Segment_E, Segment2.Segment_E, Arduino1.D12/MISO
  N2: Segment1.Segment_D, Segment2.Segment_D, Arduino1.D11_PWM/MOSI
  N3: Segment1.common_anode, Q2.C
  N4: Segment1.Segment_C, Segment2.Segment_C, Arduino1.D9_PWM
  N5: Segment1.Segment_DP, Segment2.Segment_DP, Arduino1.D8
  N6: Segment1.Segment_B, Segment2.Segment_B, Arduino1.D3_PWM
  N7: Segment1.Segment_A, Segment2.Segment_A, Arduino1.D4
  N8: Segment1.Segment_F, Segment2.Segment_F, Arduino1.D5_PWM
  N9: Segment1.Segment_G, Segment2.Segment_G, Arduino1.D6_PWM
  N10: Segment2.common_anode, Q3.C
  N11: R1.Pin_0, Q1.B
  N12: R1.Pin_1, Arduino1.D10_PWM/SS
  N13: R2.Pin_0, Q1.C
  N14: R2.Pin_1, Q2.B
  N15: R3.Pin_0, Arduino1.D7
  N16: R3.Pin_1, Q4.B
  N17: R4.Pin_0, Q4.C
  N18: R4.Pin_1, Q3.B
  N19: S1.Pin_1, S1.Pin_2, Q3.E, Q2.E, Arduino1.5V
  N20: S1.Pin_3, S1.Pin_4, R5.Pin_1, Arduino1.D2
  N21: R5.Pin_0, Q4.E, Q1.E, R6.wiper, Arduino1.GND
  N22: R6.leg1, Arduino1.A1
  N23: R6.leg2, Arduino1.A0
