# Fritzing sketch LED-Matrix (saved by Fritzing 0.7.0b)
breadboards: 1

parts:
  Arduino1 = Arduino
  R1 = Resistor [tolerance=±5% resistance=1k package=THT]
  R2 = Resistor [tolerance=±5% resistance=1k package=THT]
  R3 = Resistor [tolerance=±5% resistance=1k package=THT]
  R4 = Resistor [tolerance=±5% resistance=1k package=THT]
  R5 = Resistor [tolerance=±5% resistance=1k package=THT]
  Dot_Matrix = LED Dot Matrix 18mm (0.7 INCH)
  Q1 = PNP-Transistor [package="TO92 [THT]"]
  Q2 = PNP-Transistor [package="TO92 [THT]"]
  Q3 = PNP-Transistor [package="TO92 [THT]"]
  Q4 = PNP-Transistor [package="TO92 [THT]"]
  Q5 = PNP-Transistor [package="TO92 [THT]"]

nets:
  N1: Arduino1.D12, Dot_Matrix.Row_1
  N2: Arduino1.D11, Dot_Matrix.Row_2
  N3: Arduino1.D10, R1.Pin_0
  N4: Arduino1.D9, Dot_Matrix.Row_4
  N5: Arduino1.D8, R2.Pin_0
  N6: Arduino1.D7, R3.Pin_0
  N7: Arduino1.D6, Dot_Matrix.Row_7
  N8: Arduino1.D5, Dot_Matrix.Row_6
  N9: Arduino1.D4, Dot_Matrix.Row_5
  N10: Arduino1.D3, R4.Pin_0
  N11: Arduino1.D2, Dot_Matrix.Row_3
  N12: Arduino1.D1TX, R5.Pin_0
  N13: Arduino1.+5V, Q1.E, Q2.E, Q3.E, Q4.E, Q5.E
  N14: R1.Pin_1, Q1.B
  N15: R2.Pin_1, Q2.B
  N16: R3.Pin_1, Q3.B
  N17: R4.Pin_1, Q4.B
  N18: R5.Pin_1, Q5.B
  N19: Dot_Matrix.Column_1, Q5.C
  N20: Dot_Matrix.Column_2, Q4.C
  N21: Dot_Matrix.Column_4, Q3.C
  N22: Dot_Matrix.Column_5, Q2.C
  N23: Dot_Matrix.Column_3, Q1.C

notes:
  Sketch by Johannes Findeisen
  www.hanez.org
  Find the Code here:
  Code
