# Fritzing sketch RGB-LED (saved by Fritzing 0.7.0b)
breadboards: 1

parts:
  R1 = Resistor [resistance=180 tolerance=±5% package=THT]
  R3 = Resistor [resistance=100 tolerance=±5% package=THT]
  R2 = Resistor [resistance=100 tolerance=±5% package=THT]
  LED1 = RGB LED - (4 legs) [package="5 mm [THT]"]
  RGB_Shield = Arduino

nets:
  N1: R1.Pin_0, RGB_Shield.D11
  N2: R1.Pin_1, LED1.red_cathode
  N3: R3.Pin_0, RGB_Shield.D9
  N4: R3.Pin_1, LED1.blue_cathode
  N5: R2.Pin_0, RGB_Shield.D10
  N6: R2.Pin_1, LED1.green_cathode
  N7: LED1.common_anode, RGB_Shield.+5V

notes:
  Let the light shine in any color!
  Check out this forum post for a good code example.
