# Fritzing sketch Sabotage-Detection (saved by Fritzing 0.7.0b)
breadboards: 1

parts:
  S1 = Pushbutton [package="[THT]"]
  R1 = Resistor [tolerance=±5% resistance=220 package=THT]
  R2 = Resistor [tolerance=±5% resistance=220 package=THT]
  R3 = Resistor [tolerance=±5% resistance=1.1k package=THT]
  R4 = Resistor [tolerance=±5% resistance=220 package=THT]
  LED3 = LED - 5mm [color="Green (555nm)" package="5 mm [THT]"]
  R5 = Rotary Potentiometer (Small) [maximum_resistance=10kΩ]
  Bauteil1 = Triple Axis Accelerometer Breakout - ADXL335
  Arduino1 = Arduino
  LED4 = Super Flux LED blue [color=Blue]
  LED5 = Super Flux LED blue [color=Red]

nets:
  N1: S1.Pin_1, S1.Pin_2, R5.leg1, Arduino1.+5V
  N2: S1.Pin_3, S1.Pin_4, R3.Pin_1, Arduino1.D2
  GND: R1.Pin_0, R2.Pin_0, R3.Pin_0, R4.Pin_0, R5.leg2, Bauteil1.GND, Arduino1.GND
  N3: R1.Pin_1, LED4.cathode
  N4: R2.Pin_1, LED5.cathode
  N5: R4.Pin_1, LED3.cathode
  N6: LED3.anode, Arduino1.D11
  N7: R5.wiper, Arduino1.A3
  N8: Bauteil1.ZOUT, Arduino1.A0
  N9: Bauteil1.YOUT, Arduino1.A1
  N10: Bauteil1.XOUT, Arduino1.A2
  VCC: Bauteil1.VCC, Arduino1.3V3
  N11: Arduino1.D7, LED4.anode
  N12: Arduino1.D3, LED5.anode

notes:
  Get the Arduino Code from here:
  Sabotage Alert

// code stored in the sketch: Sabotage-Detection.ino
/*
  _____       .__  __         .__                
_/ ____\______|__|/  |________|__| ____    ____  
\   __\\_  __ \  \   __\___   /  |/    \  / ___\ 
 |  |   |  | \/  ||  |  /    /|  |   |  \/ /_/  >
 |__|   |__|  |__||__| /_____ \__|___|  /\___  / 
                             \/       \//_____/  
  
Example      Sabotage Detection
Autor        Stefan Hermann
Date         5.12.2011

*/

int myState=0;
int greenLedPin=11;
int redLedPin=7;
int blueLedPin=3;
int buttonPin=2;
int potPin=3;
int accZPin=0;
int accYPin=1;
int accXPin=2;

int startAccZ;
int startAccY;
int startAccX;

void setup(){
  pinMode(greenLedPin,OUTPUT);
  pinMode(redLedPin,OUTPUT);
  pinMode(blueLedPin,OUTPUT);
  pinMode(buttonPin,INPUT);
  startAccZ=analogRead(accZPin);
  startAccY=analogRead(accYPin);
  startAccX=analogRead(accXPin);
}

void alertBlinking(){
  digitalWrite(redLedPin,HIGH);
  delay(50);
  digitalWrite(redLedPin,LOW);
  delay(100);
  digitalWrite(blueLedPin,HIGH);
  delay(50);
  digitalWrite(blueLedPin,LOW); 
  delay(100);  
}

boolean senseAcceleration(int myPotVal){
  boolean myReturn=false;
  myPotVal=map(myPotVal,0,1023,0,10);
  if (analogRead(accXPin)>startAccX+myPotVal) myReturn=true;
  if (analogRead(accYPin)>startAccY+myPotVal) myReturn=true;
  if (analogRead(accZPin)>startAccZ+myPotVal) myReturn=true;
  return myReturn;
}

void loop(){
  //alertBlinking();
  switch (myState){
  case 0: //idle
    if (senseAcceleration(analogRead(potPin))==true) {
      digitalWrite(greenLedPin,LOW);
      myState=1;
    } else {
      digitalWrite(greenLedPin,HIGH);    
    };
    break;
  case 1: // alert
    alertBlinking();
    if (digitalRead(buttonPin)==HIGH){
      myState=0;
    }
    break;
  }
  delay(10);
}
