# Fritzing sketch TiltSwitch (saved by Fritzing 0.8.5b)
circuit board: 6.88566cm x 5.36311cm
breadboards: 2

parts:
  Arduino1 = Arduino Uno (Rev3)
  Switch = Tilt Switch [package=THT]
  R1 = Resistor [tolerance=±5% resistance=100k package=THT]

nets:
  N1: Arduino1.GND, R1.Pin_0
  N2: Arduino1.D2, Switch.Pin_1, R1.Pin_1
  N3: Arduino1.5V, Switch.Pin_2

notes:
  In this example, a tilt switch is used (just like a button) as a digital input, and an LED is a digital output. The resistor is a pull-down resistor.
  Related example: http://www.arduino.cc/en/Tutorial/TiltSensor
