# Fritzing sketch VirtualColorMixer (saved by Fritzing 0.8.0b)
breadboards: 2

parts:
  R2 = Rotary Potentiometer (Small)
  Arduino1 = Arduino Uno (Rev3)
  R1 = Rotary Potentiometer (Small)
  R3 = Rotary Potentiometer (Small)

nets:
  N1: R2.leg1, Arduino1.GND, R1.leg1, R3.leg1
  N2: R2.wiper, Arduino1.A1
  N3: R2.leg2, Arduino1.5V, R1.leg2, R3.leg2
  N4: Arduino1.A0, R1.wiper
  N5: Arduino1.A2, R3.wiper

notes:
  You can send multiple values from the Arduino board to the computer using the serial print function. In this project, the analog values from three potentiometers are used to set the red, green, and blue values of the background color of a Processing sketch running on the computer.
  http://arduino.cc/en/Tutorial/VirtualColorMixer
