# Fritzing sketch Window_Alarm (saved by Fritzing 0.7.0b)
breadboards: 1

parts:
  Speaker = Piezo Speaker
  R2 = Resistor [resistance=10k tolerance=±5% package=THT]
  Reed_Switch = Reed switch [package=THT]
  Arduino2 = Arduino

nets:
  N1: Speaker.pin1, R2.Pin_1, Arduino2.GND
  N2: Speaker.pin2, Arduino2.D9
  N3: R2.Pin_0, Reed_Switch.pin_1, Arduino2.D12
  N4: Reed_Switch.pin_2, Arduino2.+5V

notes:
  Reed switches close when a magnet is placed near their casing. In this example, a magnet could be mounted on a window and the reed switch on the windowsill so that everytime the window was opened, the piezo buzzer would sound.
  http://arduino.cc/en/Tutorial/Button
  http://arduino.cc/en/Tutorial/Melody
