# Fritzing sketch color-fader (saved by Fritzing 0.8.5b)
circuit board: 6.88566cm x 5.36311cm
circuit board: 6.88566cm x 5.36311cm
breadboards: 2

parts:
  R1 = Resistor [tolerance=±5% resistance=220 package=THT]
  Arduino1 = Arduino Uno (Rev3)
  LED1 = RGB LED (com. anode, rbg) [package="5 mm [THT]"]
  R3 = Resistor [tolerance=±5% resistance=220 package=THT]
  R2 = Resistor [tolerance=±5% resistance=220 package=THT]
  Arduino2 = Arduino Uno (Rev3)
  R5 = Resistor [tolerance=±5% resistance=220 package=THT]
  R6 = Resistor [tolerance=±5% resistance=220 package=THT]
  R7 = Resistor [tolerance=±5% resistance=220 package=THT]
  LED2 = RGB LED (com. cathode, rbg) [package="5 mm [THT]"]
  R4 = Rotary Potentiometer (Small) [maximum_resistance=100kΩ package=THT]
  R8 = Rotary Potentiometer (Small) [maximum_resistance=100kΩ package=THT]

nets:
  N1: R1.Pin_0, LED1.red_cathode
  N2: R1.Pin_1, Arduino1.D11_PWM/MOSI
  N3: Arduino1.A0, R4.wiper
  N4: Arduino1.D9_PWM, R2.Pin_1
  N5: Arduino1.D10_PWM/SS, R3.Pin_1
  N6: Arduino1.5V, LED1.common_anode, R4.leg2
  N7: Arduino1.GND, R4.leg1
  N8: LED1.blue_cathode, R3.Pin_0
  N9: LED1.green_cathode, R2.Pin_0
  N10: Arduino2.A0, R8.wiper
  N11: Arduino2.D9_PWM, R7.Pin_1
  N12: Arduino2.D10_PWM/SS, R6.Pin_1
  N13: Arduino2.D11_PWM/MOSI, R5.Pin_1
  N14: Arduino2.GND, LED2.common_cathode, R8.leg1
  N15: Arduino2.5V, R8.leg2
  N16: R5.Pin_0, LED2.red_anode
  N17: R6.Pin_0, LED2.blue_anode
  N18: R7.Pin_0, LED2.green_anode

notes:
  A potentiometer is used to display rainbow colors on an rgb LED.
  Get the Arduino-Code from here:
  http://fritzing.org/projects/color-fader/
  This is the same example, but using a "common cathode" RGB LED.
  Note that its long pin connects to - instead of +.
  This example is using the type in the Fritzing Starter Kits (pins: blue, common cathode, red, green).
